# Fritzing sketch schematics (saved by Fritzing 0.9.0b)

parts:
  part = Arduino Uno (Rev3)
  R1 = Resistor [tolerance=±5% resistance=10k package="0603 [SMD]"]
  Magnetic_reed_switch = SWITCH-MOMENTARY-2 [package=reed_switch_pth]

nets:
  N1: part.D8, R1.Pin_1, Magnetic_reed_switch.1
  N2: part.GND, R1.Pin_0
  N3: part.5V, Magnetic_reed_switch.2

notes:
  Pulldown resistor. ~10KOhm
  Magnetic reed switch
